// Logisim project seq_circuit 유정훈.circ as structural Verilog: 1 circuit, main circuit main
module main (
  input  X,
  input  Y
);

  wire and_1_out, and_2_out, d_ff_1_q, or_1_out, undriven, xor_1_out, xor_2_out;

  xor xor_1 (xor_1_out, X, Y);
  and and_1 (and_1_out, X, Y);
  xor xor_2 (xor_2_out, xor_1_out, d_ff_1_q);
  and and_2 (and_2_out, xor_1_out, d_ff_1_q);
  Clock clock_1 ();  // open: out
  or or_1 (or_1_out, and_2_out, and_1_out);
  D_Flip_Flop d_ff_1 (.clk(undriven), .D(or_1_out), .Q(d_ff_1_q));  // open: Qn, preset, en, reset

  // Notes on the sheet:
  //   Q
  //   S
  //   C
  //   D Flip Flop
endmodule
