// Logisim project seq_circuit 정훈.circ as structural Verilog: 1 circuit, main circuit main
module main (
  input  X,
  input  Y
);

  wire clock_1_out, D_q, undriven, undriven_2;

  \seq_circuit_유정훈_main  main_1 (.X(undriven), .Y(undriven_2));
  Clock clock_1 (.out(clock_1_out));
  D_Flip_Flop D (.clk(clock_1_out), .D(undriven_2), .Q(D_q));  // open: Qn, preset, en, reset

  // Notes on the sheet:
  //   C
  //   Clock
  //   S
endmodule
